# Fritzing sketch ax-12a-bench-test (saved by Fritzing 1.0.7)
breadboards: 2

parts:
  Adafruit_Feather_ESP32-C1 = Adafruit Feather ESP32-C6 [mn=Adafruit mpn=#5933 part_number=#5933]
  AX-12A_Motor = Header 3 [package=jst-3-smd]
  MEAN_WELL_LRS-50-12_12V_IN_Power_Supply = Screw terminal - 2 pins [package=THT]
  IC2 = 74LVC245 Octal 2-Way Tranceiver
  R4 = Resistor [tolerance=±5% resistance=2.2k package="2010 [SMD]"]
  R5 = Resistor [tolerance=±5% resistance=1k package="2010 [SMD]"]

nets:
  N1: Adafruit_Feather_ESP32-C1.IO15, IC2.A1
  N2: Adafruit_Feather_ESP32-C1.IO14, IC2.A2, R4.Pin_0, R5.Pin_0, R5.Pin_1
  N3: Adafruit_Feather_ESP32-C1.IO8, IC2.DIR
  N4: AX-12A_Motor.1, MEAN_WELL_LRS-50-12_12V_IN_Power_Supply.pin1
  N5: IC2.GND, IC2.!OE, R4.Pin_1
  N6: IC2.B2, IC2.B1

notes:
  file: ax-12a-bench-test.fzz
  version: 1
  last updated: 14 July 2026 20:47
  author: Willem van Heemstra
  +12 Volt
  +5 Volt
